// Logisim project p1.circ as structural Verilog
module main (
  input  a,
  input  b,
  input  in_3,
  input  in_4,
  input  c,
  input  in_6,
  input  in_7,
  input  d,
  output out_9,
  output out_10,
  output out_11,
  output out_12
);

  wire and_1_out, logic_test_1_out1, logic_test_1_out2, or_1_out;

  logic_test logic_test_1 (.a(in_3), .b(in_4), .c(in_6), .d(in_7), .out1(logic_test_1_out1), .out2(logic_test_1_out2));
  and and_1 (and_1_out, a, b, c, d);
  or or_1 (or_1_out, a, b, c, d);
endmodule

// VHDL entity logic_test, as the project stores it:
--library and package
library ieee;
use ieee.std_logic_1164.all;
use ieee.std_logic_arith.all;
use ieee.std_logic_unsigned.all;

--entity
entity logic_test is
    port(
        a,b,c,d   :in  std_logic;
        out1,out2 :out std_logic
    );
end entity logic_test;

--architecture
architecture bhv of logic_test is
begin
    out1 <= a and b and c and d;
    out2 <= a or b or c or d;
end architecture bhv;
