// Logisim project p2.circ as structural Verilog
module main (
  input  a,
  input  in_2,
  input  b,
  input  in_4,
  input  in_5,
  input  c,
  input  in_7,
  input  in_8,
  input  d,
  input  in_10,
  input  in_11,
  input  in_12,
  input  e,
  input  [2:0] in_14,
  input  f,
  input  g,
  input  h,
  input  ch0,
  input  ch1,
  input  ch2,
  output out_21,
  output data
);

  wire and_1_out, and_2_out, and_3_out, and_4_out, and_5_out, and_6_out, and_7_out, and_8_out, mux8_1_1_data,
       not_1_out, not_2_out, not_3_out, not_4_out, not_5_out, not_6_out, not_7_out, not_8_out, not_9_out,
       not_10_out, not_11_out, not_12_out;

  mux8_1 mux8_1_1 (
    .a(in_2), .b(in_4), .c(in_5), .d(in_7), .e(in_8), .f(in_10), .g(in_11), .h(in_12), .ch(in_14),
    .data(mux8_1_1_data));
  not not_1 (not_1_out, ch0);
  not not_2 (not_2_out, ch0);
  not not_3 (not_3_out, ch0);
  not not_4 (not_4_out, ch0);
  not not_5 (not_5_out, ch1);
  not not_6 (not_6_out, ch1);
  not not_7 (not_7_out, ch1);
  not not_8 (not_8_out, ch1);
  not not_9 (not_9_out, ch2);
  not not_10 (not_10_out, ch2);
  not not_11 (not_11_out, ch2);
  not not_12 (not_12_out, ch2);
  and and_1 (and_1_out, a, not_1_out, not_5_out, not_9_out);
  and and_2 (and_2_out, b, ch0, not_6_out, not_10_out);
  and and_3 (and_3_out, c, not_2_out, ch1, not_11_out);
  and and_4 (and_4_out, d, ch0, ch1, not_12_out);
  and and_5 (and_5_out, e, not_3_out, not_7_out, ch2);
  and and_6 (and_6_out, f, ch0, not_8_out, ch2);
  and and_7 (and_7_out, g, not_4_out, ch1, ch2);
  and and_8 (and_8_out, h, ch0, ch1, ch2);
  or or_1 (data, and_1_out, and_2_out, and_3_out, and_4_out, and_5_out, and_6_out, and_7_out, and_8_out);
endmodule

// VHDL entity mux8_1, as the project stores it:
--library and package
library ieee;
use ieee.std_logic_1164.all;
use ieee.std_logic_arith.all;
use ieee.std_logic_unsigned.all;

--entity
entity mux8_1 is
    port(
        a,b,c,d,e,f,g,h :in  std_logic;
        ch              :in  std_logic_vector(2 downto 0);
        data            :out std_logic
    );
end entity mux8_1;

--architecture
architecture bhv of mux8_1 is
begin
    process(a,b,c,d,e,f,g,h,ch)
    begin
        case ch is
            when "000" => data <= a;
            when "001" => data <= b;
            when "010" => data <= c;
            when "011" => data <= d;
            when "100" => data <= e;
            when "101" => data <= f;
            when "110" => data <= g;
            when "111" => data <= h;
            when others => data <= '0';
        end case;
    end process;
end architecture bhv;
