// Logisim project p3.circ as structural Verilog
module main (
  input  in_1,
  input  [3:0] in_2
);

  wire [7:0] led_letter_1_display;

  led_letter led_letter_1 (.en(in_1), .dat(in_2), .display(led_letter_1_display));
  _7_Segment_Display u_7_segment_display_1 (
    .g(led_letter_1_display[1]), .f(led_letter_1_display[2]), .a(led_letter_1_display[7]),
    .b(led_letter_1_display[6]), .e(led_letter_1_display[3]), .d(led_letter_1_display[4]),
    .c(led_letter_1_display[5]), .dp(led_letter_1_display[0]));
endmodule

// VHDL entity led_letter, as the project stores it:
--library and package
library ieee;
use ieee.std_logic_1164.all;
use ieee.std_logic_arith.all;
use ieee.std_logic_unsigned.all;

--entity
entity led_letter is
    port(
        en      :in  std_logic;
        dat     :in  std_logic_vector(3 downto 0);
        display :out std_logic_vector(7 downto 0)
    );
end entity led_letter;

--architecture
--display = a b c d e f g dp
architecture bhv of led_letter is
begin
    process(en,dat)
    begin
        if en='0' then
            display <= "ZZZZZZZZ";
        else
            case dat is
                when "0000" => display <= "11101110";  --a
                when "0001" => display <= "00111110";  --b
                when "0010" => display <= "10011100";  --c
                when "0011" => display <= "01111010";  --d
                when "0100" => display <= "10001110";  --f
                when "0101" => display <= "11110110";  --g
                when others => display <= "00000000";
            end case;
        end if;
    end process;
end architecture bhv;
