// Logisim project p5.circ as structural Verilog
module main (
  input  in_1
);

  wire [7:0] vote_led_1_display;
  wire [12:0] dipswitch_1_p13;

  // DipSwitch #(.number(13)) dipswitch_1: pin names not known; wires that end beside it: dipswitch_1_p13[12], dipswitch_1_p13[11], dipswitch_1_p13[10], dipswitch_1_p13[9], dipswitch_1_p13[8], dipswitch_1_p13[7], dipswitch_1_p13[6], dipswitch_1_p13[5], dipswitch_1_p13[4], dipswitch_1_p13[3], dipswitch_1_p13[2], dipswitch_1_p13[1], dipswitch_1_p13[0]
  vote_led vote_led_1 (.vt(dipswitch_1_p13), .en(in_1), .display(vote_led_1_display));
  _7_Segment_Display u_7_segment_display_1 (
    .g(vote_led_1_display[1]), .f(vote_led_1_display[2]), .a(vote_led_1_display[7]),
    .b(vote_led_1_display[6]), .e(vote_led_1_display[3]), .d(vote_led_1_display[4]),
    .c(vote_led_1_display[5]), .dp(vote_led_1_display[0]));
endmodule

// VHDL entity vote_led, as the project stores it:
--library and package
library ieee;
use ieee.std_logic_1164.all;
use ieee.std_logic_arith.all;
use ieee.std_logic_unsigned.all;

--entity
entity vote_led is
    port(
        vt      :in  std_logic_vector(13 downto 1);
        en      :in  std_logic;
        display :out std_logic_vector(7 downto 0)
    );
end entity vote_led;

--architecture
--display = a b c d e f g dp
architecture bhv of vote_led is
begin
    process(vt,en)
        variable sum:integer range 0 to 15;
    begin
        sum:= 0;
        for i in 1 to 13 loop
            if (vt(i)='1') then
                sum:=sum+1;
            end if;
        end loop;
        if en='0' then
            display <= "ZZZZZZZZ";
        else
            case sum is
                when 0  => display <= "11111100";  --0
                when 1  => display <= "01100000";  --1
                when 2  => display <= "11011010";  --2
                when 3  => display <= "11110010";  --3
                when 4  => display <= "01100110";  --4
                when 5  => display <= "10110110";  --5
                when 6  => display <= "10111110";  --6
                when 7  => display <= "11100000";  --7
                when 8  => display <= "11111110";  --8
                when 9  => display <= "11100110";  --9
                when 10 => display <= "11101110";  --A
                when 11 => display <= "00111110";  --B
                when 12 => display <= "10011100";  --C
                when 13 => display <= "01111010";  --D
                when 14 => display <= "10011110";  --E
                when 15 => display <= "10001110";  --F
                when others => display <= "00000000";
            end case;
        end if;
    end process;
end architecture bhv;
